# Fritzing sketch arroseur (saved by Fritzing 0.9.3b)
breadboards: 1

parts:
  Composant1 = DeuLigne 1.1 - The Snootlab's LCD shield for Arduino
  R1 = Resistor [tolerance=±5% resistance=100k package=THT]
  VALVE1 = Plastic Solenoid Valve
  Alimentation_12v = Power plug
  TIP102G = npn-Powertransistor [package="TO220 [THT]"]
  R2 = Resistor [tolerance=±5% resistance=2.2k package=THT]  # not connected
  D1 = Rectifier Diode [part_number=1N4001 package="300 mil [THT]"]  # not connected

nets:
  N1: Composant1.+5V, R1.Pin_0
  GND: Composant1.GND, Alimentation_12v.GND, TIP102G.emitter
  N2: Composant1.A1, R1.Pin_1
  N3: VALVE1.no_name_yet#1, Alimentation_12v.VCC
  N4: VALVE1.no_name_yet#2, TIP102G.collector
